// Logisim project Logisim 8.2.1.circ as structural Verilog: 5 circuits, main circuit bcd_to_binary
module main (
  input  in_1,
  input  in_2,
  input  in_3,
  input  in_4,
  input  in_5,
  input  in_6,
  input  in_7,
  input  in_8,
  input  in_9,
  input  [5:0] in_10,
  input  in_11,
  input  in_12,
  input  in_13,
  input  in_14,
  input  in_15,
  input  in_16,
  input  in_17,
  input  in_18,
  input  in_19,
  input  [1:0] in_20,
  input  [1:0] in_21,
  output [23:0] out_22,
  output [31:0] out_23,
  output [31:0] out_24,
  output [31:0] out_25,
  output [31:0] out_26,
  output [31:0] out_27,
  output [31:0] out_28,
  output [17:0] out_29,
  output [5:0] out_30,
  output out_31,
  output out_32,
  output out_33,
  output out_34,
  output out_35,
  output out_36,
  output out_37,
  output out_38,
  output [31:0] out_39,
  output out_40,
  output out_41,
  output out_42,
  output out_43,
  output out_44,
  output out_45,
  output out_46,
  output out_47
);

  wire and_2_out, and_3_out, and_4_out, and_5_out, and_6_out, and_8_out, and_9_out, and_10_out, and_11_out,
       and_12_out, and_13_out, and_14_out, and_18_out, and_24_out, and_28_out, and_29_out, and_30_out,
       and_31_out, and_32_out, and_33_out, and_34_out, and_35_out, and_38_out, and_39_out, and_40_out,
       and_41_out, and_42_out, and_43_out, and_44_out, and_45_out, and_46_out, and_50_out, and_51_out,
       and_52_out, and_53_out, and_56_out, and_57_out, and_62_out, and_63_out, and_65_out, and_82_out,
       and_83_out, and_84_out, and_85_out, and_86_out, and_87_out, and_88_out, and_89_out, and_108_out,
       and_109_out, and_110_out, and_111_out, and_112_out, and_113_out, clocksys_out, clrregs,
       comparator_1_lt, comparator_3_eq, comparator_3_lt, comparator_4_eq, comparator_4_gt, comparator_5_lt,
       comparator_6_gt, comparator_7_eq, comparator_8_eq, d_ff_1_q, d_ff_2_q, d_ff_3_q, d_ff_4_q, d_ff_4_qn,
       d_ff_6_q, d_ff_6_qn, d_ff_15_q, d_ff_17_q, d_ff_18_q, d_ff_19_q, d_ff_21_q, d_ff_22_q, d_ff_23_q,
       d_ff_24_q, d_ff_25_q, d_ff_26_q, d_ff_28_q, d_ff_29_q, d_ff_30_q, d_ff_35_q, d_ff_36_q, d_ff_37_q,
       d_ff_38_q, d_ff_39_q, d_ff_40_q, d_ff_41_q, enable_print_2_out, enable_print_3_out,
       enable_print_4_out, enable_print_5_out, enable_print_out, keyboard_2_avail, keyboard_3_avail,
       keyboard_4_avail, multiplexer_4_out, multiplexer_5_out, not_1_out, not_2_out, not_3_out, not_4_out,
       not_6_out, not_7_out, not_8_out, not_9_out, not_10_out, not_11_out, not_12_out, not_13_out,
       not_14_out, not_15_out, not_16_out, not_17_out, not_18_out, not_19_out, not_20_out, not_21_out,
       not_22_out, not_23_out, not_25_out, not_26_out, not_27_out, or_2_out, or_4_out, or_5_out, or_6_out,
       or_10_out, or_11_out, or_12_out, or_13_out, or_14_out, or_15_out, or_20_out, or_21_out, or_23_out,
       or_24_out, or_25_out, or_26_out, or_27_out, or_29_out, or_33_out, or_34_out, or_35_out, or_36_out,
       or_37_out, or_38_out, or_48_out, or_49_out, or_50_out, or_51_out, or_52_out, or_53_out, or_54_out,
       or_55_out, register_1_q, register_2_q, register_13_q, register_15_q, sp_hp_star, undriven,
       update_sp_2_out, update_sp_3_out, update_sp_out, update_stack_clock_before_out, use_mem1_for_r2_out,
       write_data_at_addess_of_sp_to_reg_mem_1_out;
  wire [0:0] or_58_out;
  wire [1:0] or_17_out;
  wire [2:0] and_1_out, hp3;
  wire [6:0] d_ff_9_q, keyboard_3_data, keyboard_4_data;
  wire [7:0] and_58_out, and_59_out, and_60_out, and_61_out, or_40_out, ram_2_data;
  wire [7:7] d_ff_31_q, d_ff_32_q, d_ff_33_q, d_ff_34_q;
  wire [15:0] adder_1_out, adder_2_out, adder_4_out, adder_5_out, adder_6_out, and_7_out, and_16_out,
       and_17_out, and_19_out, and_23_out, and_25_out, and_26_out, and_27_out, and_36_out, and_37_out,
       and_54_out, and_55_out, and_64_out, and_81_out, dir_dec_out, dir_inc_out, dir_wr_out, mem_dec_r1_out,
       mem_inc_r1_out, mem_wr_r1_out, multiplexer_1_out, multiplexer_2_out, multiplexer_3_out, or_8_out,
       or_9_out, or_18_out, or_19_out, or_22_out, or_32_out, or_41_out, or_47_out, pop_out, push_out,
       register_5_q, register_6_q, register_7_q_2, register_16_q, subtractor_1_out, subtractor_2_out,
       subtractor_3_out, subtractor_4_out, subtractor_5_out, subtractor_6_out, subtractor_7_out;
  wire [15:15] d_ff_5_q, d_ff_7_q, d_ff_8_q, d_ff_12_q, d_ff_12_qn, d_ff_27_q, d_ff_27_qn, dir_dec_2_out,
       dir_inc_2_out, mem_dec_r1_2_out, mem_inc_r1_2_out, mem_write_ri_out, not_5_out, not_24_out, or_3_out,
       pop_2_out, push_3_out, save_out, sub__r3_in_read_from_2_out, sub_wr__out_wr_r2_out,
       use_sp_to_write_out;
  wire [21:6] register_4_q;
  wire [23:0] and_20_out, and_21_out, and_22_out, ip, register_8_q, xnor_1_out;
  wire [23:23] and_15_out, reg1_jml_out, reg2_jmo_out;
  wire [31:0] adder_3_out, adder_7_out, ALU_out, and_48_out, and_49_out, and_66_out, and_67_out, and_68_out,
       and_69_out, and_70_out, and_71_out, and_72_out, and_73_out, and_74_out, and_75_out, and_76_out,
       and_77_out, and_78_out, and_79_out, and_80_out, and_90_out, and_91_out, and_92_out, and_93_out,
       and_94_out, and_95_out, and_96_out, and_97_out, and_98_out, and_99_out, and_100_out, and_101_out,
       and_102_out, and_103_out, and_104_out, and_105_out, and_106_out, and_107_out, and_114_out,
       demultiplexer_1_out0, demultiplexer_2_out0, divider_1_out, divider_2_out, keyboard_out,
       led_matrix_module_1_out_0, led_matrix_module_1_out_1, led_matrix_module_1_out_3,
       led_matrix_module_1_out_4, leyboard_out, multiplier_1_out, multiplier_2_out, negator_1_out,
       next_line_address_write_out, or_28_out, or_30_out, or_31_out, or_56_out, or_57_out, r2_out,
       register_17_q, register_18_q, register_19_q, register_20_q, shifter_1_out, shifter_2_out,
       stack_write_out, subtractor_8_out, subtractor_9_out, xnor_2_out;
  wire [31:16] register_7_q;
  wire [31:22] register_3_q;
  wire [31:24] register_8_q_2;
  wire [31:31] demultiplexer_2_out9, demultiplexer_3_out0, demultiplexer_3_out1, demultiplexer_3_out3,
       demultiplexer_3_out4, demultiplexer_3_out5, demultiplexer_3_out6, demultiplexer_3_out7,
       demultiplexer_3_out8, demultiplexer_3_out9, demultiplexer_3_out10, demultiplexer_3_out11,
       demultiplexer_3_out25, demultiplexer_3_out26, demultiplexer_3_out27, demultiplexer_3_out28,
       demultiplexer_3_out29, demultiplexer_3_out30, demultiplexer_3_out31, push_2_out, r2__as_write_out;

  or or_1 (sp_hp_star, and_1_out[2], and_1_out[1], and_1_out[0]);
  assign and_1_out = {hp3[0], hp3[1], hp3[2]} & {d_ff_8_q[15], d_ff_7_q[15], d_ff_5_q[15]};  // AND_Gate and_1, 3 bits wide
  assign xnor_1_out = ~(24'h186 ^ ip);  // XNOR_Gate xnor_1, 24 bits wide
  and and_2 (and_2_out, register_3_q[27], d_ff_5_q[15]);
  and and_3 (and_3_out, register_3_q[28], d_ff_7_q[15]);
  and and_4 (and_4_out, register_3_q[29], d_ff_8_q[15]);
  and and_5 (and_5_out, update_stack_clock_before_out, d_ff_9_q[1]);
  or or_2 (or_2_out, in_18, and_6_out);
  and and_6 (and_6_out, xnor_1_out[23], xnor_1_out[22], xnor_1_out[21], xnor_1_out[20], xnor_1_out[19], xnor_1_out[18], xnor_1_out[17], xnor_1_out[16], xnor_1_out[15], xnor_1_out[14], xnor_1_out[13], xnor_1_out[12], xnor_1_out[11], xnor_1_out[10], xnor_1_out[9], xnor_1_out[8], xnor_1_out[7], xnor_1_out[6], xnor_1_out[5], xnor_1_out[4], xnor_1_out[3], xnor_1_out[2], xnor_1_out[1], xnor_1_out[0], in_19);
  assign and_7_out = {16{or_3_out[15]}} & or_47_out;  // AND_Gate and_7, 16 bits wide
  or or_3 (or_3_out[15], and_2_out, and_3_out, and_4_out);
  or or_4 (or_4_out, and_5_out, and_8_out);
  and and_8 (and_8_out, not_1_out, clrregs);
  not not_1 (not_1_out, update_stack_clock_before_out);
  not not_2 (not_2_out, or_2_out);
  Register #(.width(1)) register_1 (.D(d_ff_9_q[3]), .Q(register_1_q), .clk(and_14_out));  // open: en, clr
  and and_9 (and_9_out, register_1_q, and_41_out);
  and and_10 (and_10_out, and_41_out, register_2_q);
  and and_11 (and_11_out, update_sp_out, or_4_out);
  not not_3 (not_3_out, and_12_out);
  and and_12 (and_12_out, or_36_out, d_ff_4_q);
  and and_13 (and_13_out, not_2_out, or_14_out);
  or or_5 (or_5_out, d_ff_1_q, d_ff_9_q[0]);
  Register #(.width(1)) register_2 (.D(d_ff_9_q[1]), .Q(register_2_q), .clk(and_14_out));  // open: en, clr
  Register #(.width(32)) register_3 (
    .D({out_23[0], out_23[1], out_23[2], out_23[3], out_23[4], out_23[5], out_23[6], out_23[7], out_23[8], out_23[9], out_23[10], out_23[11], out_23[12], out_23[13], out_23[14], out_23[15], out_23[16], out_23[17], out_23[18], out_23[19], out_23[20], out_23[21], out_23[22], out_23[23], out_23[24], out_23[25], out_23[26], out_23[27], out_23[28], out_23[29], out_23[30], out_23[31]}),
    .Q({register_3_q[31:27], hp3[0], hp3[1], hp3[2], register_3_q[23:22], out_24[0], out_24[1], out_24[2], out_24[3], out_24[4], out_24[5], out_24[6], out_24[7], out_24[8], out_24[9], out_24[10], out_24[11], out_24[12], out_24[13], out_24[14], out_24[15], out_24[16], out_24[17], out_24[18], out_24[19], out_24[20], out_24[21]}),
    .clk(d_ff_3_q));  // open: en, clr
  Register #(.width(32)) register_4 (
    .D({out_23[0], out_23[1], out_23[2], out_23[3], out_23[4], out_23[5], out_23[6], out_23[7], out_23[8], out_23[9], out_23[10], out_23[11], out_23[12], out_23[13], out_23[14], out_23[15], out_23[16], out_23[17], out_23[18], out_23[19], out_23[20], out_23[21], out_23[22], out_23[23], out_23[24], out_23[25], out_23[26], out_23[27], out_23[28], out_23[29], out_23[30], out_23[31]}),
    .Q({out_24[22], out_24[23], out_24[24], out_24[25], out_24[26], out_24[27], out_24[28], out_24[29], out_24[30], out_24[31], register_4_q, out_30[0], out_30[1], out_30[2], out_30[3], out_30[4], out_30[5]}),
    .clk(d_ff_1_q));  // open: en, clr
  D_Flip_Flop d_ff_1 (.clk(and_18_out), .D(and_13_out), .Q(d_ff_1_q));  // open: Qn, preset, en, reset
  D_Flip_Flop d_ff_2 (.clk(and_18_out), .D(d_ff_1_q), .Q(d_ff_2_q));  // open: Qn, preset, en, reset
  D_Flip_Flop d_ff_3 (.clk(and_18_out), .D(d_ff_2_q), .Q(d_ff_3_q));  // open: Qn, preset, en, reset
  D_Flip_Flop d_ff_4 (.clk(or_5_out), .D(d_ff_4_qn), .Q(d_ff_4_q), .Qn(d_ff_4_qn));  // open: preset, en, reset
  and and_14 (and_14_out, not_4_out, and_18_out);
  Adder #(.width(16)) adder_1 (
    .a({{14{1'b0}}, register_3_q[30], register_3_q[31]}), .b(16'h1), .out(adder_1_out));  // open: cin, cout
  not not_4 (not_4_out, or_25_out);
  or or_6 (or_6_out, or_25_out, d_ff_1_q, d_ff_2_q, d_ff_3_q);
  and and_15 (and_15_out[23], not_8_out, not_9_out);
  assign out_22 = and_20_out | and_21_out | and_22_out;  // OR_Gate or_7, 24 bits wide
  Multiplexer #(.width(16)) multiplexer_1 (
    .in0({register_4_q[6], register_4_q[7], register_4_q[8], register_4_q[9], register_4_q[10], register_4_q[11], register_4_q[12], register_4_q[13], register_4_q[14], register_4_q[15], register_4_q[16], register_4_q[17], register_4_q[18], register_4_q[19], register_4_q[20], register_4_q[21]}),
    .in1(register_5_q), .out(multiplexer_1_out), .sel(write_data_at_addess_of_sp_to_reg_mem_1_out));  // open: en
  assign or_8_out = and_16_out | and_17_out;  // OR_Gate or_8, 16 bits wide
  assign and_16_out = register_7_q_2 & {16{not_5_out[15]}};  // AND_Gate and_16, 16 bits wide
  not not_5 (not_5_out[15], use_sp_to_write_out[15]);
  Register #(.width(16)) register_5 (.D(or_9_out), .Q(register_5_q), .clk(and_11_out));  // open: en, clr
  assign or_9_out = mem_wr_r1_out | dir_wr_out | or_18_out | push_out | pop_out;  // OR_Gate or_9, 16 bits wide
  assign pop_out = adder_2_out & {16{pop_2_out[15]}};  // AND_Gate pop, 16 bits wide
  Adder #(.width(16)) adder_2 (.a(register_5_q), .b(adder_1_out), .out(adder_2_out));  // open: cin, cout
  assign mem_wr_r1_out = register_7_q_2 & {16{mem_write_ri_out[15]}};  // AND_Gate mem_wr_r1, 16 bits wide
  Clock clocksys (.out(clocksys_out));
  or or_10 (or_10_out, d_ff_8_q[15], d_ff_7_q[15], d_ff_5_q[15]);
  not not_6 (not_6_out, or_10_out);
  not not_7 (not_7_out, d_ff_6_q);
  not not_8 (not_8_out, reg2_jmo_out[23]);
  not not_9 (not_9_out, reg1_jml_out[23]);
  assign and_17_out = register_5_q & {16{use_sp_to_write_out[15]}};  // AND_Gate and_17, 16 bits wide
  assign push_out = subtractor_1_out & {16{push_3_out[15]}};  // AND_Gate push, 16 bits wide
  Subtractor #(.width(16)) subtractor_1 (.a(register_5_q), .b(adder_1_out), .out(subtractor_1_out));  // open: bin, bout
  D_Flip_Flop d_ff_5 (.clk(or_12_out), .D(or_11_out), .Q(d_ff_5_q[15]));  // open: Qn, preset, en, reset
  or or_11 (or_11_out, not_6_out, d_ff_8_q[15]);
  or or_12 (or_12_out, d_ff_9_q[5], d_ff_9_q[3], d_ff_9_q[1]);
  or or_13 (or_13_out, or_6_out, d_ff_9_q[5], d_ff_9_q[4], d_ff_9_q[3], d_ff_9_q[2], d_ff_9_q[1], d_ff_9_q[0], d_ff_19_q);
  and and_18 (and_18_out, clocksys_out, not_7_out);
  D_Flip_Flop d_ff_6 (.clk(and_38_out), .D(d_ff_6_qn), .Q(d_ff_6_q), .Qn(d_ff_6_qn));  // open: preset, en, reset
  Adder #(.width(32)) adder_3 (.a({register_7_q, register_7_q_2}), .b(32'h1), .out(adder_3_out));  // open: cin, cout
  Multiplexer #(.width(16)) multiplexer_2 (
    .in0(out_24[31:16]), .in1(subtractor_2_out), .out(multiplexer_2_out), .sel(use_mem1_for_r2_out));  // open: en
  Subtractor #(.width(16)) subtractor_2 (
    .a(register_7_q_2), .b(and_19_out), .out(subtractor_2_out));  // open: bin, bout
  assign and_19_out = out_24[31:16] & {16{sub__r3_in_read_from_2_out[15]}};  // AND_Gate and_19, 16 bits wide
  assign dir_wr_out = out_24[15:0] & {16{save_out[15]}};  // AND_Gate dir_wr, 16 bits wide
  D_Flip_Flop d_ff_7 (.clk(or_12_out), .D(d_ff_5_q[15]), .Q(d_ff_7_q[15]));  // open: Qn, preset, en, reset
  not not_10 (not_10_out, or_13_out);
  assign and_20_out = {24{reg2_jmo_out[23]}} & register_8_q;  // AND_Gate and_20, 24 bits wide
  assign and_21_out = {24{reg1_jml_out[23]}} & adder_3_out[23:0];  // AND_Gate and_21, 24 bits wide
  assign and_22_out = {24{and_15_out[23]}} & out_24[23:0];  // AND_Gate and_22, 24 bits wide
  assign and_23_out = out_24[15:0] & {16{sub_wr__out_wr_r2_out[15]}};  // AND_Gate and_23, 16 bits wide
  assign dir_dec_out = adder_5_out & {16{dir_dec_2_out[15]}};  // AND_Gate dir_dec, 16 bits wide
  assign mem_dec_r1_out = adder_4_out & {16{mem_dec_r1_2_out[15]}};  // AND_Gate mem_dec_r1, 16 bits wide
  Adder #(.width(16)) adder_4 (.a(register_5_q), .b(register_7_q_2), .out(adder_4_out));  // open: cin, cout
  D_Flip_Flop d_ff_8 (.clk(or_12_out), .D(d_ff_7_q[15]), .Q(d_ff_8_q[15]));  // open: Qn, preset, en, reset
  D_Flip_Flop d_ff_9 (.clk(and_18_out), .D(d_ff_3_q), .Q(d_ff_9_q[0]));  // open: Qn, preset, en, reset
  or or_14 (or_14_out, not_10_out, clrregs);
  or or_15 (or_15_out, and_24_out, and_34_out, out_29[9], and_33_out);
  and and_24 (and_24_out, and_52_out, out_29[7]);
  assign and_25_out = subtractor_3_out & {16{d_ff_8_q[15]}};  // AND_Gate and_25, 16 bits wide
  assign and_26_out = multiplexer_2_out & {16{d_ff_7_q[15]}};  // AND_Gate and_26, 16 bits wide
  assign and_27_out = multiplexer_1_out & {16{d_ff_5_q[15]}};  // AND_Gate and_27, 16 bits wide
  Multiplexer #(.select(2), .width(16)) multiplexer_3 (
    .in0(out_24[15:0]), .in1(out_24[31:16]), .in2(multiplexer_1_out), .in3(or_8_out),
    .out(multiplexer_3_out), .sel(or_17_out));  // open: en
  or or_16 (or_17_out[1], and_28_out, and_30_out);
  or or_17 (or_17_out[0], and_29_out, and_31_out);
  and and_28 (and_28_out, not_11_out, not_14_out, out_29[15]);
  and and_29 (and_29_out, out_29[16], not_14_out, out_29[15]);
  and and_30 (and_30_out, not_11_out, not_13_out, enable_print_3_out);
  and and_31 (and_31_out, not_11_out, not_13_out, enable_print_3_out);
  assign or_18_out = dir_dec_out | mem_dec_r1_out | mem_inc_r1_out | dir_inc_out;  // OR_Gate or_18, 16 bits wide
  Adder #(.width(16)) adder_5 (.a(register_5_q), .b(out_24[15:0]), .out(adder_5_out));  // open: cin, cout
  assign mem_inc_r1_out = subtractor_5_out & {16{mem_inc_r1_2_out[15]}};  // AND_Gate mem_inc_r1, 16 bits wide
  D_Flip_Flop d_ff_10 (.clk(and_18_out), .D(d_ff_9_q[0]), .Q(d_ff_9_q[1]));  // open: Qn, preset, en, reset
  and and_32 (and_32_out, not_3_out, or_15_out);
  and and_33 (and_33_out, d_ff_26_q, out_29[5]);
  and and_34 (and_34_out, and_51_out, out_29[6]);
  assign or_19_out = and_25_out | and_26_out | and_27_out;  // OR_Gate or_19, 16 bits wide
  Subtractor #(.width(16)) subtractor_3 (
    .a(multiplexer_3_out), .b(and_23_out), .out(subtractor_3_out));  // open: bin, bout
  not not_11 (not_11_out, out_29[16]);
  assign dir_inc_out = subtractor_4_out & {16{dir_inc_2_out[15]}};  // AND_Gate dir_inc, 16 bits wide
  Subtractor #(.width(16)) subtractor_4 (
    .a(register_5_q), .b(out_24[15:0]), .out(subtractor_4_out));  // open: bin, bout
  Subtractor #(.width(16)) subtractor_5 (
    .a(register_5_q), .b(register_7_q_2), .out(subtractor_5_out));  // open: bin, bout
  and and_35 (and_35_out, xnor_2_out[0], xnor_2_out[1], xnor_2_out[2], xnor_2_out[3], xnor_2_out[4], xnor_2_out[5], xnor_2_out[6], xnor_2_out[7], xnor_2_out[8], xnor_2_out[9], xnor_2_out[10], xnor_2_out[11], xnor_2_out[12], xnor_2_out[13], xnor_2_out[14], xnor_2_out[15], xnor_2_out[17], xnor_2_out[18], xnor_2_out[19], xnor_2_out[20], xnor_2_out[21], xnor_2_out[22], xnor_2_out[23], xnor_2_out[24], xnor_2_out[25], xnor_2_out[26], xnor_2_out[27], xnor_2_out[28], xnor_2_out[29], xnor_2_out[30], xnor_2_out[31], xnor_2_out[16]);
  D_Flip_Flop d_ff_11 (.clk(and_18_out), .D(and_10_out), .Q(d_ff_9_q[2]));  // open: Qn, preset, en, reset
  or or_20 (or_20_out, d_ff_9_q[2], d_ff_9_q[4]);
  D_Flip_Flop d_ff_12 (
    .clk(d_ff_15_q), .D(1'b1), .Q(d_ff_12_q[15]), .Qn(d_ff_12_qn[15]), .reset(or_20_out));  // open: preset, en
  assign and_36_out = adder_6_out & {16{d_ff_12_qn[15]}};  // AND_Gate and_36, 16 bits wide
  Counter #(.width(24), .max('hffffff)) counter_1 (
    .load(and_32_out), .D(out_22), .count(not_12_out), .Q(ip), .clk(or_21_out));  // open: carry, clr
  not not_12 (not_12_out, and_32_out);
  or or_21 (or_21_out, d_ff_2_q, clrregs);
  Adder #(.width(16)) adder_6 (.a(and_7_out), .b(or_19_out), .out(adder_6_out));  // open: cin, cout
  not not_13 (not_13_out, out_29[15]);
  not not_14 (not_14_out, enable_print_3_out);
  D_Flip_Flop d_ff_13 (.clk(and_18_out), .D(d_ff_9_q[2]), .Q(d_ff_9_q[3]));  // open: Qn, preset, en, reset
  assign and_37_out = {16{d_ff_12_q[15]}} & subtractor_6_out;  // AND_Gate and_37, 16 bits wide
  assign or_22_out = and_36_out | and_37_out;  // OR_Gate or_22, 16 bits wide
  or or_23 (or_23_out, d_ff_9_q[1], d_ff_9_q[3], and_40_out);
  or or_24 (or_24_out, d_ff_15_q, d_ff_17_q, d_ff_18_q);
  or or_25 (or_25_out, or_24_out, or_34_out);
  D_Flip_Flop d_ff_14 (.clk(and_18_out), .D(and_9_out), .Q(d_ff_9_q[4]));  // open: Qn, preset, en, reset
  and and_38 (and_38_out, d_ff_9_q[5], out_29[12], not_15_out);
  Subtractor #(.width(16)) subtractor_6 (.a(register_6_q), .b(16'h1), .out(subtractor_6_out));  // open: bin, bout
  Register #(.width(16)) register_6 (.D(or_22_out), .Q(register_6_q), .clk(d_ff_15_q), .clr(or_20_out));  // open: en
  D_Flip_Flop d_ff_15 (.clk(and_18_out), .D(or_23_out), .Q(d_ff_15_q), .reset(or_20_out));  // open: Qn, preset, en
  D_Flip_Flop d_ff_16 (.clk(and_18_out), .D(d_ff_9_q[4]), .Q(d_ff_9_q[5]));  // open: Qn, preset, en, reset
  not not_15 (not_15_out, and_87_out);
  D_Flip_Flop d_ff_17 (.clk(and_18_out), .D(d_ff_15_q), .Q(d_ff_17_q), .reset(or_20_out));  // open: Qn, preset, en
  and and_39 (and_39_out, d_ff_19_q, out_29[17]);
  D_Flip_Flop d_ff_18 (.clk(and_18_out), .D(d_ff_17_q), .Q(d_ff_18_q), .reset(or_20_out));  // open: Qn, preset, en
  not not_16 (not_16_out, multiplexer_4_out);
  and and_40 (and_40_out, d_ff_18_q, not_16_out);
  RAM #(.addrWidth(16), .dataWidth(16), .bus("separate")) ram_1 (.clk(and_39_out));  // open: addr, din, data, str, sel, ld, clr
  not not_17 (not_17_out, out_30[5]);
  Demultiplexer #(.select(5)) demultiplexer_1 (
    .out0(demultiplexer_1_out0[0]), .out1(demultiplexer_1_out0[1]), .out2(demultiplexer_1_out0[2]),
    .out3(demultiplexer_1_out0[3]), .out4(demultiplexer_1_out0[4]), .out5(demultiplexer_1_out0[5]),
    .out6(demultiplexer_1_out0[6]), .out7(demultiplexer_1_out0[7]), .out8(demultiplexer_1_out0[8]),
    .out9(demultiplexer_1_out0[9]), .out10(demultiplexer_1_out0[10]), .out11(demultiplexer_1_out0[11]),
    .out12(demultiplexer_1_out0[12]), .out13(demultiplexer_1_out0[13]), .out14(demultiplexer_1_out0[14]),
    .out15(demultiplexer_1_out0[15]), .out16(demultiplexer_1_out0[16]), .out17(demultiplexer_1_out0[17]),
    .out18(demultiplexer_1_out0[18]), .out19(demultiplexer_1_out0[19]), .out20(demultiplexer_1_out0[20]),
    .out21(demultiplexer_1_out0[21]), .out22(demultiplexer_1_out0[22]), .out23(demultiplexer_1_out0[23]),
    .out24(demultiplexer_1_out0[24]), .out25(demultiplexer_1_out0[25]), .out26(demultiplexer_1_out0[26]),
    .out27(demultiplexer_1_out0[27]), .out28(demultiplexer_1_out0[28]), .out29(demultiplexer_1_out0[29]),
    .out30(demultiplexer_1_out0[30]), .out31(demultiplexer_1_out0[31]), .in(not_17_out), .sel(out_30[4:0]));  // open: en
  Demultiplexer #(.select(5)) demultiplexer_2 (
    .out0(demultiplexer_2_out0[0]), .out1(demultiplexer_2_out0[1]), .out2(demultiplexer_2_out0[2]),
    .out3(demultiplexer_2_out0[3]), .out4(demultiplexer_2_out0[4]), .out5(demultiplexer_2_out0[5]),
    .out6(demultiplexer_2_out0[6]), .out7(demultiplexer_2_out0[7]), .out8(demultiplexer_2_out0[8]),
    .out9(demultiplexer_2_out9[31]), .out10(demultiplexer_2_out0[10]), .out11(demultiplexer_2_out0[11]),
    .out12(demultiplexer_2_out0[12]), .out13(demultiplexer_2_out0[13]), .out14(demultiplexer_2_out0[14]),
    .out15(demultiplexer_2_out0[15]), .out16(demultiplexer_2_out0[16]), .out17(demultiplexer_2_out0[17]),
    .out18(demultiplexer_2_out0[18]), .out19(demultiplexer_2_out0[19]), .out20(demultiplexer_2_out0[20]),
    .out21(demultiplexer_2_out0[21]), .out22(demultiplexer_2_out0[22]), .out23(demultiplexer_2_out0[23]),
    .out24(demultiplexer_2_out0[24]), .out25(demultiplexer_2_out0[25]), .out26(demultiplexer_2_out0[26]),
    .out27(demultiplexer_2_out0[27]), .out28(demultiplexer_2_out0[28]), .out29(demultiplexer_2_out0[29]),
    .out30(demultiplexer_2_out0[30]), .out31(demultiplexer_2_out0[31]), .in(out_30[5]), .sel(out_30[4:0]));  // open: en
  D_Flip_Flop d_ff_19 (.clk(and_18_out), .D(d_ff_9_q[5]), .Q(d_ff_19_q));  // open: Qn, preset, en, reset
  D_Flip_Flop d_ff_20 (.clk(and_18_out), .D(d_ff_9_q[6]), .Q(clrregs));  // open: Qn, preset, en, reset
  and and_41 (and_41_out, d_ff_18_q, multiplexer_4_out);
  or use_sp_to_write (use_sp_to_write_out[15], demultiplexer_2_out0[10], demultiplexer_2_out0[0], demultiplexer_2_out0[2], demultiplexer_1_out0[31]);
  or or_26 (or_26_out, not_18_out, d_ff_24_q);
  ROM #(.addrWidth(24), .dataWidth(32)) rom_1 (.addr(ip), .data(out_23));  // open: sel
  or or_27 (or_27_out, demultiplexer_2_out0[23], demultiplexer_2_out0[24], demultiplexer_2_out0[25], demultiplexer_2_out0[30]);
  or use_mem1_for_r2 (use_mem1_for_r2_out, demultiplexer_2_out0[14], demultiplexer_2_out0[15], demultiplexer_2_out0[19], demultiplexer_2_out0[16]);
  or update_stack_clock_before (update_stack_clock_before_out, demultiplexer_2_out0[16], demultiplexer_2_out0[17], demultiplexer_2_out0[1]);
  Register #(.width(32)) register_7 (
    .D(out_28), .Q({register_7_q, register_7_q_2}), .clk(d_ff_9_q[2]));  // open: en, clr
  Register #(.width(32)) register_8 (
    .D(out_28), .Q({register_8_q_2, register_8_q}), .clk(d_ff_9_q[4]));  // open: en, clr
  D_Flip_Flop d_ff_21 (.clk(d_ff_17_q), .D(or_26_out), .Q(d_ff_21_q), .reset(or_20_out));  // open: Qn, preset, en
  D_Flip_Flop d_ff_22 (.clk(d_ff_17_q), .D(d_ff_21_q), .Q(d_ff_22_q), .reset(or_20_out));  // open: Qn, preset, en
  D_Flip_Flop d_ff_23 (.clk(d_ff_17_q), .D(d_ff_22_q), .Q(d_ff_23_q), .reset(or_20_out));  // open: Qn, preset, en
  D_Flip_Flop d_ff_24 (.clk(d_ff_17_q), .D(d_ff_23_q), .Q(d_ff_24_q), .reset(or_20_out));  // open: Qn, preset, en
  assign or_28_out = leyboard_out | keyboard_out | or_31_out | r2_out | ALU_out;  // OR_Gate or_28, 32 bits wide
  or sub_wr__out_wr_r2 (sub_wr__out_wr_r2_out[15], demultiplexer_2_out0[15], demultiplexer_2_out0[18], demultiplexer_2_out0[13]);
  Register register_9 (.D(ram_2_data), .Q(out_28[7:0]), .clk(and_42_out), .clr(clrregs));  // open: en
  and and_42 (and_42_out, d_ff_21_q, d_ff_18_q);
  Register register_10 (.D(ram_2_data), .Q(out_28[15:8]), .clk(and_43_out), .clr(clrregs));  // open: en
  and and_43 (and_43_out, d_ff_22_q, d_ff_18_q);
  Register register_11 (.D(ram_2_data), .Q(out_28[23:16]), .clk(and_44_out), .clr(clrregs));  // open: en
  and and_44 (and_44_out, d_ff_23_q, d_ff_18_q);
  Register register_12 (.D(ram_2_data), .Q(out_28[31:24]), .clk(and_45_out), .clr(clrregs));  // open: en
  and and_45 (and_45_out, d_ff_24_q, d_ff_18_q);
  assign leyboard_out = {{25{1'b0}}, out_26[6:0]} & {32{out_29[13]}};  // AND_Gate leyboard, 32 bits wide
  assign ALU_out = {32{out_29[14]}} & out_39;  // AND_Gate ALU, 32 bits wide
  assign r2_out = {32{r2__as_write_out[31]}} & {register_8_q_2, register_8_q};  // AND_Gate r2, 32 bits wide
  or write_en (out_29[17], or_27_out, demultiplexer_1_out0[1], demultiplexer_1_out0[2], demultiplexer_1_out0[3], demultiplexer_1_out0[4], demultiplexer_1_out0[5], demultiplexer_1_out0[6], demultiplexer_1_out0[7], demultiplexer_1_out0[8], demultiplexer_1_out0[9], demultiplexer_1_out0[10], demultiplexer_1_out0[11], demultiplexer_1_out0[17], demultiplexer_1_out0[18], demultiplexer_1_out0[23], demultiplexer_1_out0[30], demultiplexer_1_out0[31], demultiplexer_2_out0[0], demultiplexer_2_out0[2], demultiplexer_2_out9[31], demultiplexer_2_out0[10], demultiplexer_2_out0[13], demultiplexer_2_out0[14], demultiplexer_2_out0[15], demultiplexer_2_out0[18], demultiplexer_2_out0[19], demultiplexer_2_out0[1], demultiplexer_2_out0[22], demultiplexer_2_out0[26], demultiplexer_2_out0[27], demultiplexer_2_out0[28], demultiplexer_2_out0[29]);
  buf reg1_jml (reg1_jml_out[23], demultiplexer_2_out0[17]);  // OR_Gate
  not not_18 (not_18_out, or_29_out);
  or or_29 (or_29_out, d_ff_22_q, d_ff_23_q, d_ff_24_q, d_ff_21_q);
  Multiplexer #(.select(2)) multiplexer_4 (
    .in0(d_ff_21_q), .in1(d_ff_22_q), .in2(d_ff_23_q), .in3(d_ff_24_q), .out(multiplexer_4_out),
    .sel({register_3_q[30], register_3_q[31]}));  // open: en
  buf reg2_jmo (reg2_jmo_out[23], demultiplexer_2_out0[16]);  // OR_Gate
  // OR_Gate update_comp_reg: pin names not known; wires that end beside it: demultiplexer_1_out0[12], demultiplexer_1_out0[13], out_29[8], out_40, in_11
  assign xnor_2_out = ~({register_7_q, register_7_q_2} ^ or_30_out);  // XNOR_Gate xnor_2, 32 bits wide
  and and_46 (and_46_out, d_ff_19_q, out_29[8]);
  or write_data_at_addess_of_sp_to_reg_mem_1 (write_data_at_addess_of_sp_to_reg_mem_1_out, demultiplexer_2_out0[16], demultiplexer_2_out0[17], demultiplexer_2_out0[1]);
  D_Flip_Flop d_ff_25 (.clk(and_46_out), .D(comparator_1_lt), .Q(d_ff_25_q));  // open: Qn, preset, en, reset
  D_Flip_Flop d_ff_26 (.clk(and_46_out), .D(and_35_out), .Q(d_ff_26_q));  // open: Qn, preset, en, reset
  and and_47 (d_ff_9_q[6], register_13_q, and_57_out);
  Register #(.width(1)) register_13 (.D(d_ff_19_q), .Q(register_13_q), .clk(and_53_out));  // open: en, clr
  Register #(.width(32)) register_14 (.D({{25{1'b0}}, out_27[6:0]}), .Q(out_25), .clk(and_87_out));  // open: en, clr
  Comparator #(.width(32)) comparator_1 (
    .a({register_7_q, register_7_q_2}), .b(or_30_out), .lt(comparator_1_lt));  // open: gt, eq
  not not_19 (not_19_out, d_ff_25_q);
  not not_20 (not_20_out, d_ff_26_q);
  assign and_48_out = {register_8_q_2, register_8_q} & {32{out_29[11]}};  // AND_Gate and_48, 32 bits wide
  assign and_49_out = {32{out_29[10]}} & out_24;  // AND_Gate and_49, 32 bits wide
  and and_50 (and_50_out, and_57_out, register_15_q);
  or write_3 (out_29[16], demultiplexer_1_out0[1], demultiplexer_1_out0[2], demultiplexer_1_out0[3], demultiplexer_1_out0[4], demultiplexer_1_out0[5], demultiplexer_2_out0[14], demultiplexer_2_out0[15], demultiplexer_2_out0[19], demultiplexer_2_out0[1], demultiplexer_2_out0[22], demultiplexer_2_out0[23], demultiplexer_2_out0[24], demultiplexer_2_out0[25], demultiplexer_2_out0[26], demultiplexer_2_out0[27], demultiplexer_2_out0[28], demultiplexer_2_out0[29], demultiplexer_2_out0[30]);
  // OR_Gate if_grter: pin names not known; wires that end beside it: in_11, demultiplexer_1_out0[14], out_29[7], out_41, in_12
  and and_51 (and_51_out, d_ff_25_q, not_20_out);
  and and_52 (and_52_out, not_20_out, not_19_out);
  assign or_30_out = and_48_out | and_49_out;  // OR_Gate or_30, 32 bits wide
  Comparator #(.width(2)) comparator_2 (.a(in_20), .b(in_21), .lt(out_47));  // open: gt, eq
  and and_53 (and_53_out, not_21_out, and_18_out);
  Register #(.width(1)) register_15 (.D(in_1), .Q(register_15_q), .clk(and_53_out));  // open: en, clr
  assign keyboard_out = out_25 & {32{out_29[12]}};  // AND_Gate keyboard, 32 bits wide
  not not_21 (not_21_out, or_34_out);
  assign or_31_out = next_line_address_write_out | stack_write_out;  // OR_Gate or_31, 32 bits wide
  buf sub__r3_in_read_from_2 (sub__r3_in_read_from_2_out[15], demultiplexer_2_out0[19]);  // OR_Gate
  assign next_line_address_write_out = {{8{1'b0}}, ip} & {32{push_2_out[31]}};  // AND_Gate next_line_address_write, 32 bits wide
  D_Flip_Flop d_ff_27 (
    .clk(d_ff_28_q), .D(1'b1), .Q(d_ff_27_q[15]), .Qn(d_ff_27_qn[15]), .reset(clrregs));  // open: preset, en
  assign and_54_out = adder_6_out & {16{d_ff_27_qn[15]}};  // AND_Gate and_54, 16 bits wide
  assign and_55_out = {16{d_ff_27_q[15]}} & subtractor_7_out;  // AND_Gate and_55, 16 bits wide
  assign or_32_out = and_54_out | and_55_out;  // OR_Gate or_32, 16 bits wide
  or write_1 (out_29[15], demultiplexer_1_out0[6], demultiplexer_1_out0[7], demultiplexer_1_out0[8], demultiplexer_1_out0[9], demultiplexer_1_out0[10], demultiplexer_1_out0[11], demultiplexer_1_out0[17], demultiplexer_1_out0[18], demultiplexer_2_out9[31], demultiplexer_2_out0[13]);
  // OR_Gate if_less: pin names not known; wires that end beside it: in_12, demultiplexer_1_out0[15], out_29[6], out_42, in_13
  Subtractor #(.width(16)) subtractor_7 (.a(register_16_q), .b(16'h1), .out(subtractor_7_out));  // open: bin, bout
  Register #(.width(16)) register_16 (.D(or_32_out), .Q(register_16_q), .clk(d_ff_28_q), .clr(clrregs));  // open: en
  D_Flip_Flop d_ff_28 (.clk(and_18_out), .D(or_33_out), .Q(d_ff_28_q), .reset(clrregs));  // open: Qn, preset, en
  or or_33 (or_33_out, in_1, d_ff_19_q, and_56_out);
  or or_34 (or_34_out, d_ff_28_q, d_ff_29_q, d_ff_30_q);
  D_Flip_Flop d_ff_29 (.clk(and_18_out), .D(d_ff_28_q), .Q(d_ff_29_q), .reset(clrregs));  // open: Qn, preset, en
  or or_35 (or_35_out, demultiplexer_2_out0[30], demultiplexer_2_out0[29], demultiplexer_1_out0[1]);
  or or_36 (or_36_out, out_29[7], out_29[6], out_29[5], out_29[9]);
  D_Flip_Flop d_ff_30 (.clk(and_18_out), .D(d_ff_29_q), .Q(d_ff_30_q), .reset(clrregs));  // open: Qn, preset, en
  not not_22 (not_22_out, multiplexer_5_out);
  and and_56 (and_56_out, d_ff_30_q, not_22_out);
  and and_57 (and_57_out, d_ff_30_q, multiplexer_5_out);
  assign stack_write_out = {{16{1'b0}}, register_5_q} & {32{demultiplexer_2_out9[31]}};  // AND_Gate stack_write, 32 bits wide
  or alu_write (out_29[14], or_35_out, demultiplexer_1_out0[2], demultiplexer_1_out0[3], demultiplexer_1_out0[4], demultiplexer_1_out0[5], demultiplexer_1_out0[6], demultiplexer_1_out0[7], demultiplexer_1_out0[8], demultiplexer_1_out0[9], demultiplexer_1_out0[10], demultiplexer_1_out0[11], demultiplexer_1_out0[12], demultiplexer_1_out0[13], demultiplexer_1_out0[19], demultiplexer_1_out0[20], demultiplexer_1_out0[22], demultiplexer_1_out0[23], demultiplexer_1_out0[24], demultiplexer_1_out0[25], demultiplexer_1_out0[28], demultiplexer_1_out0[29], demultiplexer_2_out0[0], demultiplexer_2_out0[2], demultiplexer_2_out0[1], demultiplexer_2_out0[22], demultiplexer_2_out0[23], demultiplexer_2_out0[24], demultiplexer_2_out0[25], demultiplexer_2_out0[26], demultiplexer_2_out0[27], demultiplexer_2_out0[28]);
  or or_37 (or_37_out, not_23_out, d_ff_34_q[7]);
  // OR_Gate if_eql: pin names not known; wires that end beside it: in_13, demultiplexer_1_out0[16], out_29[5], out_43, in_14
  D_Flip_Flop d_ff_31 (.clk(d_ff_29_q), .D(or_37_out), .Q(d_ff_31_q[7]), .reset(clrregs));  // open: Qn, preset, en
  D_Flip_Flop d_ff_32 (.clk(d_ff_29_q), .D(d_ff_31_q[7]), .Q(d_ff_32_q[7]), .reset(clrregs));  // open: Qn, preset, en
  D_Flip_Flop d_ff_33 (.clk(d_ff_29_q), .D(d_ff_32_q[7]), .Q(d_ff_33_q[7]), .reset(clrregs));  // open: Qn, preset, en
  D_Flip_Flop d_ff_34 (.clk(d_ff_29_q), .D(d_ff_33_q[7]), .Q(d_ff_34_q[7]), .reset(clrregs));  // open: Qn, preset, en
  or or_38 (or_38_out, d_ff_32_q[7], d_ff_33_q[7], d_ff_34_q[7], d_ff_31_q[7]);
  Multiplexer #(.select(2)) multiplexer_5 (
    .in0(d_ff_31_q[7]), .in1(d_ff_32_q[7]), .in2(d_ff_33_q[7]), .in3(d_ff_34_q[7]), .out(multiplexer_5_out),
    .sel({register_3_q[30], register_3_q[31]}));  // open: en
  assign and_58_out = or_28_out[7:0] & {8{d_ff_31_q[7]}};  // AND_Gate and_58, 8 bits wide
  assign and_59_out = or_28_out[15:8] & {8{d_ff_32_q[7]}};  // AND_Gate and_59, 8 bits wide
  assign and_60_out = or_28_out[23:16] & {8{d_ff_33_q[7]}};  // AND_Gate and_60, 8 bits wide
  assign and_61_out = or_28_out[31:24] & {8{d_ff_34_q[7]}};  // AND_Gate and_61, 8 bits wide
  not not_23 (not_23_out, or_38_out);
  buf event_listener (out_29[13], demultiplexer_1_out0[17]);  // OR_Gate
  or or_39 (out_29[4], demultiplexer_1_out0[1], demultiplexer_1_out0[2], demultiplexer_1_out0[3], demultiplexer_1_out0[6], demultiplexer_1_out0[7], demultiplexer_1_out0[8], demultiplexer_1_out0[9], demultiplexer_1_out0[12], demultiplexer_1_out0[13], demultiplexer_1_out0[4], demultiplexer_1_out0[20], demultiplexer_1_out0[22], demultiplexer_1_out0[23], demultiplexer_1_out0[25], demultiplexer_1_out0[29], demultiplexer_2_out0[2]);
  assign or_40_out = and_58_out | and_59_out | and_60_out | and_61_out;  // OR_Gate or_40, 8 bits wide
  assign or_41_out = register_16_q | register_6_q;  // OR_Gate or_41, 16 bits wide
  and and_62 (and_62_out, d_ff_30_q, out_29[17]);
  RAM #(.addrWidth(16), .bus("separate")) ram_2 (
    .addr(or_41_out), .din(or_40_out), .data(ram_2_data), .clk(and_62_out));  // open: str, sel, ld, clr
  buf user_input (out_29[12], demultiplexer_1_out0[18]);  // OR_Gate
  or or_42 (out_29[3], demultiplexer_1_out0[1], demultiplexer_1_out0[2], demultiplexer_1_out0[3], demultiplexer_1_out0[6], demultiplexer_1_out0[7], demultiplexer_1_out0[8], demultiplexer_1_out0[9], demultiplexer_1_out0[12], demultiplexer_1_out0[13], demultiplexer_1_out0[4], demultiplexer_1_out0[20], demultiplexer_1_out0[22], demultiplexer_1_out0[23], demultiplexer_1_out0[25], demultiplexer_1_out0[29], demultiplexer_2_out0[2], demultiplexer_2_out0[27], demultiplexer_2_out0[28], demultiplexer_2_out0[29], demultiplexer_2_out0[30]);
  TTY #(.rows(40), .cols(120)) tty_1 (
    .data(or_28_out[6:0]), .clk(d_ff_19_q), .we(enable_print_5_out), .clr(and_84_out));
  or reg_read (out_29[11], demultiplexer_1_out0[1], demultiplexer_1_out0[2], demultiplexer_1_out0[3], demultiplexer_1_out0[4], demultiplexer_1_out0[5], demultiplexer_1_out0[12], demultiplexer_2_out0[22], demultiplexer_2_out0[23], demultiplexer_2_out0[24], demultiplexer_2_out0[25], demultiplexer_2_out0[26], demultiplexer_2_out0[27], demultiplexer_2_out0[28], demultiplexer_2_out0[29], demultiplexer_2_out0[30]);
  or or_43 (out_29[2], demultiplexer_1_out0[1], demultiplexer_1_out0[2], demultiplexer_1_out0[3], demultiplexer_1_out0[6], demultiplexer_1_out0[7], demultiplexer_1_out0[8], demultiplexer_1_out0[9], demultiplexer_1_out0[12], demultiplexer_1_out0[13], demultiplexer_1_out0[4], demultiplexer_1_out0[20], demultiplexer_1_out0[22], demultiplexer_1_out0[23], demultiplexer_1_out0[25], demultiplexer_1_out0[29], demultiplexer_2_out0[2], demultiplexer_2_out0[23], demultiplexer_2_out0[24], demultiplexer_2_out0[25], demultiplexer_2_out0[26]);
  or direct_read (out_29[10], demultiplexer_1_out0[6], demultiplexer_1_out0[7], demultiplexer_1_out0[8], demultiplexer_1_out0[9], demultiplexer_1_out0[10], demultiplexer_1_out0[11], demultiplexer_1_out0[13], demultiplexer_1_out0[19], demultiplexer_1_out0[20], demultiplexer_1_out0[22], demultiplexer_1_out0[23], demultiplexer_1_out0[24], demultiplexer_1_out0[25], demultiplexer_1_out0[28], demultiplexer_1_out0[29], demultiplexer_2_out0[0], demultiplexer_2_out0[2], demultiplexer_2_out0[1]);
  or or_44 (out_29[1], demultiplexer_1_out0[1], demultiplexer_1_out0[2], demultiplexer_1_out0[6], demultiplexer_1_out0[7], demultiplexer_1_out0[12], demultiplexer_1_out0[13], demultiplexer_1_out0[20], demultiplexer_1_out0[22], demultiplexer_1_out0[23], demultiplexer_1_out0[25], demultiplexer_1_out0[29], demultiplexer_2_out0[2], demultiplexer_2_out0[22], demultiplexer_2_out0[25], demultiplexer_2_out0[26], demultiplexer_2_out0[29], demultiplexer_2_out0[30]);
  or jmp (out_29[9], demultiplexer_1_out0[26], demultiplexer_2_out0[10], demultiplexer_2_out0[16], demultiplexer_2_out0[17]);
  Keyboard keyboard_2 (.clk(and_88_out), .avail(keyboard_2_avail), .data(out_27[6:0]));  // open: re, clr
  or or_45 (out_29[0], demultiplexer_1_out0[1], demultiplexer_1_out0[3], demultiplexer_1_out0[5], demultiplexer_1_out0[6], demultiplexer_1_out0[8], demultiplexer_1_out0[10], demultiplexer_1_out0[20], demultiplexer_1_out0[22], demultiplexer_1_out0[23], demultiplexer_1_out0[25], demultiplexer_1_out0[29], demultiplexer_2_out0[2], demultiplexer_2_out0[4], demultiplexer_2_out0[1], demultiplexer_2_out0[22], demultiplexer_2_out0[24], demultiplexer_2_out0[26], demultiplexer_2_out0[28], demultiplexer_2_out0[30]);
  or push_2 (push_2_out[31], demultiplexer_1_out0[31], demultiplexer_2_out0[10]);
  or r2__as_write (r2__as_write_out[31], demultiplexer_2_out0[19], demultiplexer_1_out0[30], demultiplexer_2_out0[13], demultiplexer_2_out0[14], demultiplexer_2_out0[15], demultiplexer_2_out0[18]);
  or push_3 (push_3_out[15], demultiplexer_1_out0[31], demultiplexer_2_out0[0], demultiplexer_2_out0[2], demultiplexer_2_out0[10]);
  or pop_2 (pop_2_out[15], demultiplexer_2_out0[1], demultiplexer_2_out0[17], demultiplexer_2_out0[16]);
  buf save (save_out[15], demultiplexer_2_out0[3]);  // OR_Gate
  or update_sp (update_sp_out, demultiplexer_2_out0[2], demultiplexer_2_out0[6], demultiplexer_2_out0[5], demultiplexer_2_out0[0], demultiplexer_2_out0[8], demultiplexer_2_out0[1], demultiplexer_2_out0[3], demultiplexer_2_out0[4], update_sp_2_out);
  or update_sp_2 (update_sp_2_out, demultiplexer_2_out0[7], demultiplexer_2_out0[16], demultiplexer_2_out0[10], demultiplexer_1_out0[31], update_sp_3_out);
  buf dir_dec_2 (dir_dec_2_out[15], demultiplexer_2_out0[7]);  // OR_Gate
  buf dir_inc_2 (dir_inc_2_out[15], demultiplexer_2_out0[5]);  // OR_Gate
  buf mem_write_ri (mem_write_ri_out[15], demultiplexer_2_out0[4]);  // OR_Gate
  and and_63 (and_63_out, demultiplexer_2_out0[21], clrregs);
  buf update_sp_3 (update_sp_3_out, demultiplexer_2_out0[17]);  // OR_Gate
  buf mem_dec_r1_2 (mem_dec_r1_2_out[15], demultiplexer_2_out0[8]);  // OR_Gate
  buf mem_inc_r1_2 (mem_inc_r1_2_out[15], demultiplexer_2_out0[6]);  // OR_Gate
  Register #(.width(32)) register_17 (
    .D({register_7_q, register_7_q_2}), .Q(register_17_q), .clk(and_63_out));  // open: en, clr
  assign and_64_out = register_17_q[15:0] & {16{sp_hp_star}};  // AND_Gate and_64, 16 bits wide
  and and_65 (and_65_out, clrregs, demultiplexer_2_out0[20]);
  not not_24 (not_24_out[15], sp_hp_star);
  assign and_66_out = {register_7_q, register_7_q_2} & {32{demultiplexer_3_out1[31]}};  // AND_Gate and_66, 32 bits wide
  assign and_67_out = {register_7_q, register_7_q_2} & {32{demultiplexer_3_out25[31]}};  // AND_Gate and_67, 32 bits wide
  assign and_68_out = or_30_out & {32{demultiplexer_3_out0[31]}};  // AND_Gate and_68, 32 bits wide
  assign and_69_out = {register_7_q, register_7_q_2} & {32{demultiplexer_3_out26[31]}};  // AND_Gate and_69, 32 bits wide
  assign and_70_out = {32{demultiplexer_3_out26[31]}} & or_30_out;  // AND_Gate and_70, 32 bits wide
  assign and_71_out = {register_7_q, register_7_q_2} & {32{demultiplexer_3_out27[31]}};  // AND_Gate and_71, 32 bits wide
  assign and_72_out = {32{demultiplexer_3_out27[31]}} & or_30_out;  // AND_Gate and_72, 32 bits wide
  assign and_73_out = {register_7_q, register_7_q_2} & {32{demultiplexer_3_out28[31]}};  // AND_Gate and_73, 32 bits wide
  assign and_74_out = {32{demultiplexer_3_out28[31]}} & or_30_out;  // AND_Gate and_74, 32 bits wide
  assign and_75_out = {register_7_q, register_7_q_2} & {32{demultiplexer_3_out29[31]}};  // AND_Gate and_75, 32 bits wide
  assign and_76_out = {32{demultiplexer_3_out29[31]}} & or_30_out;  // AND_Gate and_76, 32 bits wide
  assign and_77_out = {register_7_q, register_7_q_2} & {32{demultiplexer_3_out30[31]}};  // AND_Gate and_77, 32 bits wide
  assign and_78_out = {32{demultiplexer_3_out30[31]}} & or_30_out;  // AND_Gate and_78, 32 bits wide
  assign and_79_out = {register_7_q, register_7_q_2} & {32{demultiplexer_3_out31[31]}};  // AND_Gate and_79, 32 bits wide
  assign and_80_out = {32{demultiplexer_3_out31[31]}} & or_30_out;  // AND_Gate and_80, 32 bits wide
  assign out_39 = adder_7_out | subtractor_8_out | multiplier_1_out | divider_1_out | shifter_2_out | shifter_1_out | negator_1_out | and_68_out | and_66_out | or_57_out;  // OR_Gate or_46, 32 bits wide
  Register #(.width(32)) register_18 (
    .D({register_7_q, register_7_q_2}), .Q(register_18_q), .clk(and_65_out));  // open: en, clr
  Negator #(.width(32)) negator_1 (.in(and_67_out), .out(negator_1_out));
  Divider #(.width(32)) divider_1 (.a(and_73_out), .b(and_74_out), .out(divider_1_out));  // open: upper, rem
  Multiplier #(.width(32)) multiplier_1 (.a(and_75_out), .b(and_76_out), .out(multiplier_1_out));  // open: cin, cout
  Subtractor #(.width(32)) subtractor_8 (.a(and_77_out), .b(and_78_out), .out(subtractor_8_out));  // open: bin, bout
  Adder #(.width(32)) adder_7 (.a(and_79_out), .b(and_80_out), .out(adder_7_out));  // open: cin, cout
  assign and_81_out = {16{not_24_out[15]}} & register_18_q[15:0];  // AND_Gate and_81, 16 bits wide
  assign or_47_out = and_64_out | and_81_out;  // OR_Gate or_47, 16 bits wide
  Shifter #(.width(32), .shift("lr")) shifter_1 (.in(and_69_out), .\dist (and_70_out[4:0]), .out(shifter_1_out));
  Shifter #(.width(32)) shifter_2 (.in(and_71_out), .\dist (and_72_out[4:0]), .out(shifter_2_out));
  or enable_print (enable_print_out, demultiplexer_2_out0[1], demultiplexer_2_out0[10], demultiplexer_2_out0[18]);
  or enable_print_2 (enable_print_2_out, demultiplexer_1_out0[28], demultiplexer_1_out0[29]);
  LED led_1 (.in(clrregs));
  LED led_2 (.in(d_ff_9_q[5]));
  LED led_3 (.in(d_ff_9_q[6]));
  or enable_print_3 (enable_print_3_out, demultiplexer_2_out0[2], demultiplexer_1_out0[30], demultiplexer_2_out0[0], demultiplexer_1_out0[31], enable_print_out);
  or enable_print_4 (enable_print_4_out, demultiplexer_1_out0[24], demultiplexer_1_out0[25]);
  and and_82 (and_82_out, demultiplexer_1_out0[22], d_ff_9_q[6]);
  LED led_4 (.in(d_ff_9_q[3]));
  LED led_5 (.in(d_ff_9_q[1]));
  LED led_6 (.in(d_ff_9_q[4]));
  LED led_7 (.in(d_ff_9_q[2]));
  or enable_print_5 (enable_print_5_out, demultiplexer_1_out0[19], demultiplexer_1_out0[20]);
  and and_83 (and_83_out, d_ff_19_q, enable_print_4_out);
  Register #(.width(32)) register_19 (.D(or_28_out), .Q(register_19_q), .clk(and_82_out));  // open: en, clr
  LED led_8 (.in(d_ff_9_q[0]));
  led_matrix_module led_matrix_module_1 (
    .clk(and_83_out), .inp_0(or_28_out[0]), .inp1(or_28_out[1]), .inp2(or_28_out[2]), .inp3(or_28_out[3]),
    .inp_4(or_28_out[4]), .inp_5(or_28_out[5]), .inp_6(or_28_out[6]), .High_Low(or_28_out[7]),
    .out_4(led_matrix_module_1_out_4), .out_0(led_matrix_module_1_out_0), .out_1(led_matrix_module_1_out_1),
    .out_3(led_matrix_module_1_out_3));
  and and_84 (and_84_out, d_ff_19_q, demultiplexer_1_out0[21]);
  Demultiplexer #(.select(5)) demultiplexer_3 (
    .out0(demultiplexer_3_out0[31]), .out1(demultiplexer_3_out1[31]), .out3(demultiplexer_3_out3[31]),
    .out4(demultiplexer_3_out4[31]), .out5(demultiplexer_3_out5[31]), .out6(demultiplexer_3_out6[31]),
    .out7(demultiplexer_3_out7[31]), .out8(demultiplexer_3_out8[31]), .out9(demultiplexer_3_out9[31]),
    .out10(demultiplexer_3_out10[31]), .out11(demultiplexer_3_out11[31]), .out25(demultiplexer_3_out25[31]),
    .out26(demultiplexer_3_out26[31]), .out27(demultiplexer_3_out27[31]), .out28(demultiplexer_3_out28[31]),
    .out29(demultiplexer_3_out29[31]), .out30(demultiplexer_3_out30[31]), .out31(demultiplexer_3_out31[31]),
    .in(1'b1), .sel(out_29[4:0]));  // open: out2, out12, out13, out14, out15, out16, out17, out18, out19, out20, out21, out22, out23, out24, en
  or or_48 (or_48_out, not_25_out, d_ff_38_q);
  or or_49 (or_49_out, keyboard_2_avail, d_ff_37_q);
  not not_25 (not_25_out, or_51_out);
  Register #(.width(32)) register_20 (.D(or_28_out), .Q(register_20_q), .clk(and_85_out));  // open: en, clr
  and and_85 (and_85_out, enable_print_2_out, d_ff_9_q[6]);
  or or_50 (or_50_out, out_29[12], d_ff_37_q);
  and and_86 (and_86_out, or_50_out, or_49_out, clocksys_out);
  D_Flip_Flop d_ff_35 (.clk(and_86_out), .D(or_48_out), .Q(d_ff_35_q));  // open: Qn, preset, en, reset
  or or_51 (or_51_out, d_ff_38_q, d_ff_36_q, d_ff_35_q);
  and and_87 (and_87_out, d_ff_35_q, keyboard_2_avail);
  and and_88 (and_88_out, d_ff_37_q, keyboard_2_avail);
  D_Flip_Flop d_ff_36 (.clk(and_86_out), .D(d_ff_35_q), .Q(d_ff_36_q));  // open: Qn, preset, en, reset
  D_Flip_Flop d_ff_37 (.clk(and_86_out), .D(d_ff_36_q), .Q(d_ff_37_q));  // open: Qn, preset, en, reset
  D_Flip_Flop d_ff_38 (.D(d_ff_37_q), .Q(d_ff_38_q));  // open: clk, Qn, preset, en, reset
  Divider #(.width(32)) divider_2 (.a(and_90_out), .b(and_91_out), .out(divider_2_out));  // open: upper, rem
  Multiplier #(.width(32)) multiplier_2 (.a(divider_2_out), .b(and_91_out), .out(multiplier_2_out));  // open: cin, cout
  Subtractor #(.width(32)) subtractor_9 (
    .a(and_90_out), .b(multiplier_2_out), .out(subtractor_9_out));  // open: bin, bout
  or or_52 (or_52_out, not_26_out, d_ff_41_q);
  and and_89 (and_89_out, clocksys_out, keyboard_3_avail);
  not not_26 (not_26_out, or_53_out);
  Keyboard keyboard_3 (.clk(d_ff_41_q), .avail(keyboard_3_avail), .data(keyboard_3_data));  // open: re, clr
  D_Flip_Flop d_ff_39 (.clk(and_89_out), .D(or_52_out), .Q(d_ff_39_q));  // open: Qn, preset, en, reset
  or or_53 (or_53_out, d_ff_41_q, d_ff_40_q, d_ff_39_q);
  assign and_90_out = {register_7_q, register_7_q_2} & {32{demultiplexer_3_out11[31]}};  // AND_Gate and_90, 32 bits wide
  assign and_91_out = {32{demultiplexer_3_out11[31]}} & or_30_out;  // AND_Gate and_91, 32 bits wide
  assign and_92_out = {register_7_q, register_7_q_2} & {32{demultiplexer_3_out10[31]}};  // AND_Gate and_92, 32 bits wide
  assign and_93_out = {32{demultiplexer_3_out10[31]}} & or_30_out;  // AND_Gate and_93, 32 bits wide
  assign and_94_out = {register_7_q, register_7_q_2} & {32{demultiplexer_3_out9[31]}};  // AND_Gate and_94, 32 bits wide
  assign and_95_out = {32{demultiplexer_3_out9[31]}} & or_30_out;  // AND_Gate and_95, 32 bits wide
  assign and_96_out = {register_7_q, register_7_q_2} & {32{demultiplexer_3_out8[31]}};  // AND_Gate and_96, 32 bits wide
  assign and_97_out = {32{demultiplexer_3_out8[31]}} & or_30_out;  // AND_Gate and_97, 32 bits wide
  assign and_98_out = {register_7_q, register_7_q_2} & {32{demultiplexer_3_out7[31]}};  // AND_Gate and_98, 32 bits wide
  assign and_99_out = {32{demultiplexer_3_out7[31]}} & or_30_out;  // AND_Gate and_99, 32 bits wide
  assign and_100_out = {register_7_q, register_7_q_2} & {32{demultiplexer_3_out6[31]}};  // AND_Gate and_100, 32 bits wide
  assign and_101_out = {32{demultiplexer_3_out6[31]}} & or_30_out;  // AND_Gate and_101, 32 bits wide
  assign and_102_out = {register_7_q, register_7_q_2} & {32{demultiplexer_3_out5[31]}};  // AND_Gate and_102, 32 bits wide
  assign and_103_out = {32{demultiplexer_3_out5[31]}} & or_30_out;  // AND_Gate and_103, 32 bits wide
  assign and_104_out = {register_7_q, register_7_q_2} & {32{demultiplexer_3_out4[31]}};  // AND_Gate and_104, 32 bits wide
  assign and_105_out = {32{demultiplexer_3_out4[31]}} & or_30_out;  // AND_Gate and_105, 32 bits wide
  assign and_106_out = {register_7_q, register_7_q_2} & {32{demultiplexer_3_out3[31]}};  // AND_Gate and_106, 32 bits wide
  assign and_107_out = {32{demultiplexer_3_out3[31]}} & or_30_out;  // AND_Gate and_107, 32 bits wide
  D_Flip_Flop d_ff_40 (.clk(and_89_out), .D(d_ff_39_q), .Q(d_ff_40_q));  // open: Qn, preset, en, reset
  Register #(.width(7)) register_21 (
    .D(keyboard_3_data), .Q(out_26[6:0]), .clk(d_ff_39_q), .clr(demultiplexer_1_out0[27]));  // open: en
  or or_54 (or_54_out, comparator_3_eq, comparator_3_lt);
  Comparator #(.width(32)) comparator_3 (
    .a(and_92_out), .b(and_93_out), .eq(comparator_3_eq), .lt(comparator_3_lt));  // open: gt
  and and_108 (and_108_out, demultiplexer_3_out10[31], or_54_out);
  or or_55 (or_55_out, comparator_4_gt, comparator_4_eq);
  Comparator #(.width(32)) comparator_4 (
    .a(and_94_out), .b(and_95_out), .gt(comparator_4_gt), .eq(comparator_4_eq));  // open: lt
  and and_109 (and_109_out, demultiplexer_3_out9[31], or_55_out);
  Comparator #(.width(32)) comparator_5 (.a(and_96_out), .b(and_97_out), .lt(comparator_5_lt));  // open: gt, eq
  and and_110 (and_110_out, demultiplexer_3_out8[31], comparator_5_lt);
  Comparator #(.width(32)) comparator_6 (.a(and_98_out), .b(and_99_out), .gt(comparator_6_gt));  // open: eq, lt
  and and_111 (and_111_out, demultiplexer_3_out7[31], comparator_6_gt);
  not not_27 (not_27_out, comparator_7_eq);
  Comparator #(.width(32)) comparator_7 (.a(and_100_out), .b(and_101_out), .eq(comparator_7_eq));  // open: gt, lt
  and and_112 (and_112_out, demultiplexer_3_out6[31], not_27_out);
  Comparator #(.width(32)) comparator_8 (.a(and_102_out), .b(and_103_out), .eq(comparator_8_eq));  // open: gt, lt
  and and_113 (and_113_out, demultiplexer_3_out5[31], comparator_8_eq);
  assign or_56_out = and_104_out | and_105_out;  // OR_Gate or_56, 32 bits wide
  assign and_114_out = and_106_out & and_107_out;  // AND_Gate and_114, 32 bits wide
  assign or_57_out = and_114_out | or_56_out | subtractor_9_out | {{31{1'b0}}, or_58_out[0]};  // OR_Gate or_57, 32 bits wide
  D_Flip_Flop d_ff_41 (.clk(and_89_out), .D(d_ff_40_q), .Q(d_ff_41_q));  // open: Qn, preset, en, reset
  Keyboard keyboard_4 (.clk(undriven), .avail(keyboard_4_avail), .data(keyboard_4_data));  // open: re, clr
  LED led_9 (.in(led_matrix_module_1_out_0[0]));
  or or_58 (or_58_out[0], and_108_out, and_109_out, and_110_out, and_111_out, and_112_out, and_113_out);

  assign out_26[31:7] = {25{1'b0}};
  assign out_27[31:7] = {25{1'b0}};
  assign out_31 = in_2;
  assign out_32 = in_3;
  assign out_33 = in_4;
  assign out_34 = in_5;
  assign out_35 = in_6;
  assign out_36 = in_7;
  assign out_37 = in_8;
  assign out_38 = in_9;

  // Notes on the sheet:
  //   parsed size
  //   direct wr
  //   dir stack inc
  //   mem stack inc
  //   dir stack dec
  //   mem stack dec
  //   1(stack),0(ptr)
  //   contents of rom_1 (hex, n*v repeats v):
  //   8c000000 3fffc03 2c003c00 3c00 80000000 c03 a8000000 58003 48000c00 0 88001c00 3 94000000 6000
  //   a4001c00 3 d0001c00 3 94000000 3003 2c003000 1f b4003000 a000001f b4000000 3000001f 2c003000 1f
  //   b4003000 a000001f 34003000 13 3c000000 11000 40000000 11000 2c003000 281f 2c002000 1f b4002000
  //   a000000f f8002000 3000301f 88003000 1b 2c003000 c01f 84000000 2007 4002000 3000301f b7fff000
  //   3000001f 8bfff000 18 2c003000 281f 2c002000 1f b4002000 a000000f 10002000 3000301f b400a000 3000000f
  //   68000000 6800 2c003000 1f b7ffe000 3000001f 2c003000 1f b4003000 1f 34003000 13 3c000000 18800
  //   40000000 18800 840003ff ffffe004 53ffe000 1c 2c003000 281f 2c002000 1f b4002000 f 10002000 3000301f
  //   b4000000 3000000f 68000000 12000 2c003000 1f b4003000 a000001f 78009000 3000001b 68000000 1a803
  //   90001c00 3 9c000000 6003 84000000 1c03 d0001c00 1 c4000000 3 88001c00 3 94000000 6000 a4001c00 3
  //   d0001c00 3 94000000 1403 2c003000 c01c b4000000 3000001c 2c003000 1f b7fffc00 3000001f 2c003000 281f
  //   2c002000 1f b4002000 c e4002000 3000301f 34003000 13 3c000000 2d800 40000000 2d800 2c003000 281f
  //   2c002000 1f b40023ff fc00000f c002000 3000301f 88003000 1b 2c003000 1f b4003000 c 84000000 2007
  //   4002000 3000301f 88003000 1b 2c003000 c01f 84000000 2007 8002000 3000301f b7fffc00 3000000f 48000000
  //   4 50000000 1c 68000000 21800 2c003000 1f b40033ff fc00001f 78009000 3000001b 68000000 2f803 90001c00
  //   3 9c000000 6003 84000000 1c03 d0001c00 1 c4000000 3 88001c00 3 94000000 6000 a4001c00 3 d0001c00 3
  //   94000000 5003 2c003000 1f b4000000 3000001f 2c003000 41f b7fff000 3000001f 2c003000 281f 2c002000 1f
  //   b4002000 f e4002000 3000301f 34003000 13 3c000000 3e800 40000000 3e800 48000000 7 88000000 1b
  //   2c003000 41f 2c002000 1f b40023ff f000000f 4002000 3000301f b7fff000 3000000f 50000000 1c 68000000
  //   36800 2c003000 1f b40033ff f000001f 20003000 101f 4003c00 30003c0b b7ffe000 3c000017 2c003000 1f
  //   b40033ff f000001f 2c001000 1f b4001000 3000001f 2c003000 1f 200033ff fffff01f d7ffe000 1f 78003000
  //   1000003f 2c003000 41f b7ffd000 3000001f 2c003000 1f b7ffc000 3000001f 2c003000 1f b40033ff f000000f
  //   2c002000 1f b40023ff d000000f e4002000 3000301f 34003000 13 3c000000 53800 40000000 53800 840003ff
  //   ffffc007 53ffc000 1c 2c003000 1f b40033ff c000001f 2c001000 1f b4001000 3000001f 2c003000 1f
  //   b40033ff d000001f 200033ff fffff01f d7ffe000 1f 78003000 1000003f 2c003000 41f 2c002000 1f b40023ff
  //   d000000f 4002000 3000301f b7ffd000 3000000f 68000000 47000 2c003000 1f b40033ff e000001f 78009000
  //   3000001b 68000000 55803 90001c00 3 9c000000 6003 84000000 1c03 d0001c00 1 c4000000 3 88001c00 3
  //   94000000 6000 a4001c00 3 d0001c00 3 94000000 3 2c003000 1f b4003000 1c000007 18003000 301f 88003000
  //   1b a8000000 32003 9c000000 1000 78009000 3000001b 68000000 5e803 90001c00 3 9c000000 6003 84000000
  //   1c03 d0001c00 1 c4000000 3
  //   cls
  //   set copy add
  //   mov to add
  //   digital write
  //   clr el
  //   write int
  //   CLK
  //   AVALIABLE
  //   KEYBOARD CLK
  //   data
  //   CLK
  //   KEYBOARD CLK
  //   data
endmodule

module ic7476_kj (
  input  in_1,
  input  in_2,
  output out_3
);

  D_Flip_Flop d_ff_1 (.clk(in_1), .D(in_2), .Q(out_3));  // open: Qn, preset, en, reset
endmodule

module ic_74LS74 (
  input  clr1,
  input  vcc,
  input  d1,
  input  _2cls,
  input  _1clk,
  input  _2d,
  input  prs,
  input  _2clk,
  input  _2pr,
  input  gnd,
  output q1,
  output q1_star,
  output q,
  output q_star
);

  D_Flip_Flop d_ff_1 (.clk(_1clk), .D(d1), .Q(q1), .Qn(q1_star), .preset(prs), .reset(clr1));  // open: en
  D_Flip_Flop d_ff_2 (.clk(_2clk), .D(_2d), .Q(q), .Qn(q_star), .preset(_2pr), .reset(_2cls));  // open: en
endmodule

module led_matrix_module (
  input  clk,
  input  inp_0,
  input  inp1,
  input  inp2,
  input  inp3,
  input  inp_4,
  input  inp_5,
  input  inp_6,
  input  High_Low,
  output [31:0] out_4,
  output [31:0] out_0,
  output [31:0] out_1,
  output [31:0] out_3
);

  wire and_1_out, and_2_out, and_3_out, and_4_out, not_1_out, not_3_out;
  wire [31:0] and_5_out, and_6_out, and_7_out, and_8_out, and_9_out, and_10_out, and_11_out, and_12_out,
       and_13_out, and_14_out, and_15_out, and_16_out, and_17_out, and_18_out, and_19_out, and_20_out,
       demultiplexer_1_out0, demultiplexer_2_out0, demultiplexer_3_out0, demultiplexer_4_out0, not_2_out,
       not_4_out, not_5_out, not_6_out, not_7_out, not_8_out, not_9_out, not_10_out, not_11_out, not_12_out,
       not_13_out, not_14_out, or_1_out, or_2_out, or_3_out, or_4_out;

  not not_1 (not_1_out, inp_6);
  assign not_2_out = ~{32{High_Low}};  // NOT_Gate not_2, 32 bits wide
  not not_3 (not_3_out, inp_5);
  assign not_4_out = ~demultiplexer_1_out0;  // NOT_Gate not_4, 32 bits wide
  Demultiplexer #(.select(5)) demultiplexer_1 (
    .out0(demultiplexer_1_out0[0]), .out1(demultiplexer_1_out0[1]), .out2(demultiplexer_1_out0[2]),
    .out3(demultiplexer_1_out0[3]), .out4(demultiplexer_1_out0[4]), .out5(demultiplexer_1_out0[5]),
    .out6(demultiplexer_1_out0[6]), .out7(demultiplexer_1_out0[7]), .out8(demultiplexer_1_out0[8]),
    .out9(demultiplexer_1_out0[9]), .out10(demultiplexer_1_out0[10]), .out11(demultiplexer_1_out0[11]),
    .out12(demultiplexer_1_out0[12]), .out13(demultiplexer_1_out0[13]), .out14(demultiplexer_1_out0[14]),
    .out15(demultiplexer_1_out0[15]), .out16(demultiplexer_1_out0[16]), .out17(demultiplexer_1_out0[17]),
    .out18(demultiplexer_1_out0[18]), .out19(demultiplexer_1_out0[19]), .out20(demultiplexer_1_out0[20]),
    .out21(demultiplexer_1_out0[21]), .out22(demultiplexer_1_out0[22]), .out23(demultiplexer_1_out0[23]),
    .out24(demultiplexer_1_out0[24]), .out25(demultiplexer_1_out0[25]), .out26(demultiplexer_1_out0[26]),
    .out27(demultiplexer_1_out0[27]), .out28(demultiplexer_1_out0[28]), .out29(demultiplexer_1_out0[29]),
    .out30(demultiplexer_1_out0[30]), .out31(demultiplexer_1_out0[31]), .in(and_1_out),
    .sel({inp_4, inp3, inp2, inp1, inp_0}));  // open: en
  and and_1 (and_1_out, not_3_out, not_1_out);
  and and_2 (and_2_out, inp_5, not_1_out);
  and and_3 (and_3_out, not_3_out, inp_6);
  and and_4 (and_4_out, inp_5, inp_6);
  Register #(.width(32)) register_1 (.D(or_1_out), .Q(out_0), .clk(clk));  // open: en, clr
  assign not_5_out = ~out_0;  // NOT_Gate not_5, 32 bits wide
  assign and_5_out = not_2_out & not_4_out & out_0;  // AND_Gate and_5, 32 bits wide
  assign and_6_out = {32{High_Low}} & not_4_out & out_0;  // AND_Gate and_6, 32 bits wide
  assign or_1_out = and_5_out | and_6_out | and_7_out | and_8_out;  // OR_Gate or_1, 32 bits wide
  assign and_7_out = {32{High_Low}} & demultiplexer_1_out0 & not_5_out;  // AND_Gate and_7, 32 bits wide
  assign and_8_out = {32{High_Low}} & demultiplexer_1_out0 & out_0;  // AND_Gate and_8, 32 bits wide
  assign not_6_out = ~demultiplexer_2_out0;  // NOT_Gate not_6, 32 bits wide
  assign not_7_out = ~{32{High_Low}};  // NOT_Gate not_7, 32 bits wide
  Demultiplexer #(.select(5)) demultiplexer_2 (
    .out0(demultiplexer_2_out0[0]), .out1(demultiplexer_2_out0[1]), .out2(demultiplexer_2_out0[2]),
    .out3(demultiplexer_2_out0[3]), .out4(demultiplexer_2_out0[4]), .out5(demultiplexer_2_out0[5]),
    .out6(demultiplexer_2_out0[6]), .out7(demultiplexer_2_out0[7]), .out8(demultiplexer_2_out0[8]),
    .out9(demultiplexer_2_out0[9]), .out10(demultiplexer_2_out0[10]), .out11(demultiplexer_2_out0[11]),
    .out12(demultiplexer_2_out0[12]), .out13(demultiplexer_2_out0[13]), .out14(demultiplexer_2_out0[14]),
    .out15(demultiplexer_2_out0[15]), .out16(demultiplexer_2_out0[16]), .out17(demultiplexer_2_out0[17]),
    .out18(demultiplexer_2_out0[18]), .out19(demultiplexer_2_out0[19]), .out20(demultiplexer_2_out0[20]),
    .out21(demultiplexer_2_out0[21]), .out22(demultiplexer_2_out0[22]), .out23(demultiplexer_2_out0[23]),
    .out24(demultiplexer_2_out0[24]), .out25(demultiplexer_2_out0[25]), .out26(demultiplexer_2_out0[26]),
    .out27(demultiplexer_2_out0[27]), .out28(demultiplexer_2_out0[28]), .out29(demultiplexer_2_out0[29]),
    .out30(demultiplexer_2_out0[30]), .out31(demultiplexer_2_out0[31]), .in(and_2_out),
    .sel({inp_4, inp3, inp2, inp1, inp_0}));  // open: en
  Register #(.width(32)) register_2 (.D(or_2_out), .Q(out_1), .clk(clk));  // open: en, clr
  assign not_8_out = ~out_1;  // NOT_Gate not_8, 32 bits wide
  assign and_9_out = not_7_out & not_6_out & out_1;  // AND_Gate and_9, 32 bits wide
  assign and_10_out = {32{High_Low}} & not_6_out & out_1;  // AND_Gate and_10, 32 bits wide
  assign and_11_out = {32{High_Low}} & demultiplexer_2_out0 & not_8_out;  // AND_Gate and_11, 32 bits wide
  assign and_12_out = {32{High_Low}} & demultiplexer_2_out0 & out_1;  // AND_Gate and_12, 32 bits wide
  assign or_2_out = and_9_out | and_10_out | and_11_out | and_12_out;  // OR_Gate or_2, 32 bits wide
  assign not_9_out = ~{32{High_Low}};  // NOT_Gate not_9, 32 bits wide
  Register #(.width(32)) register_3 (.D(or_3_out), .Q(out_3), .clk(clk));  // open: en, clr
  assign not_10_out = ~out_3;  // NOT_Gate not_10, 32 bits wide
  assign not_11_out = ~demultiplexer_3_out0;  // NOT_Gate not_11, 32 bits wide
  Demultiplexer #(.select(5)) demultiplexer_3 (
    .out0(demultiplexer_3_out0[0]), .out1(demultiplexer_3_out0[1]), .out2(demultiplexer_3_out0[2]),
    .out3(demultiplexer_3_out0[3]), .out4(demultiplexer_3_out0[4]), .out5(demultiplexer_3_out0[5]),
    .out6(demultiplexer_3_out0[6]), .out7(demultiplexer_3_out0[7]), .out8(demultiplexer_3_out0[8]),
    .out9(demultiplexer_3_out0[9]), .out10(demultiplexer_3_out0[10]), .out11(demultiplexer_3_out0[11]),
    .out12(demultiplexer_3_out0[12]), .out13(demultiplexer_3_out0[13]), .out14(demultiplexer_3_out0[14]),
    .out15(demultiplexer_3_out0[15]), .out16(demultiplexer_3_out0[16]), .out17(demultiplexer_3_out0[17]),
    .out18(demultiplexer_3_out0[18]), .out19(demultiplexer_3_out0[19]), .out20(demultiplexer_3_out0[20]),
    .out21(demultiplexer_3_out0[21]), .out22(demultiplexer_3_out0[22]), .out23(demultiplexer_3_out0[23]),
    .out24(demultiplexer_3_out0[24]), .out25(demultiplexer_3_out0[25]), .out26(demultiplexer_3_out0[26]),
    .out27(demultiplexer_3_out0[27]), .out28(demultiplexer_3_out0[28]), .out29(demultiplexer_3_out0[29]),
    .out30(demultiplexer_3_out0[30]), .out31(demultiplexer_3_out0[31]), .in(and_3_out),
    .sel({inp_4, inp3, inp2, inp1, inp_0}));  // open: en
  assign and_13_out = not_9_out & not_11_out & out_3;  // AND_Gate and_13, 32 bits wide
  assign and_14_out = {32{High_Low}} & not_11_out & out_3;  // AND_Gate and_14, 32 bits wide
  assign and_15_out = {32{High_Low}} & demultiplexer_3_out0 & not_10_out;  // AND_Gate and_15, 32 bits wide
  assign and_16_out = {32{High_Low}} & demultiplexer_3_out0 & out_3;  // AND_Gate and_16, 32 bits wide
  assign or_3_out = and_13_out | and_14_out | and_15_out | and_16_out;  // OR_Gate or_3, 32 bits wide
  assign not_12_out = ~{32{High_Low}};  // NOT_Gate not_12, 32 bits wide
  Register #(.width(32)) register_4 (.D(or_4_out), .Q(out_4), .clk(clk));  // open: en, clr
  assign not_13_out = ~demultiplexer_4_out0;  // NOT_Gate not_13, 32 bits wide
  Demultiplexer #(.select(5)) demultiplexer_4 (
    .out0(demultiplexer_4_out0[0]), .out1(demultiplexer_4_out0[1]), .out2(demultiplexer_4_out0[2]),
    .out3(demultiplexer_4_out0[3]), .out4(demultiplexer_4_out0[4]), .out5(demultiplexer_4_out0[5]),
    .out6(demultiplexer_4_out0[6]), .out7(demultiplexer_4_out0[7]), .out8(demultiplexer_4_out0[8]),
    .out9(demultiplexer_4_out0[9]), .out10(demultiplexer_4_out0[10]), .out11(demultiplexer_4_out0[11]),
    .out12(demultiplexer_4_out0[12]), .out13(demultiplexer_4_out0[13]), .out14(demultiplexer_4_out0[14]),
    .out15(demultiplexer_4_out0[15]), .out16(demultiplexer_4_out0[16]), .out17(demultiplexer_4_out0[17]),
    .out18(demultiplexer_4_out0[18]), .out19(demultiplexer_4_out0[19]), .out20(demultiplexer_4_out0[20]),
    .out21(demultiplexer_4_out0[21]), .out22(demultiplexer_4_out0[22]), .out23(demultiplexer_4_out0[23]),
    .out24(demultiplexer_4_out0[24]), .out25(demultiplexer_4_out0[25]), .out26(demultiplexer_4_out0[26]),
    .out27(demultiplexer_4_out0[27]), .out28(demultiplexer_4_out0[28]), .out29(demultiplexer_4_out0[29]),
    .out30(demultiplexer_4_out0[30]), .out31(demultiplexer_4_out0[31]), .in(and_4_out),
    .sel({inp_4, inp3, inp2, inp1, inp_0}));  // open: en
  assign not_14_out = ~out_4;  // NOT_Gate not_14, 32 bits wide
  assign and_17_out = not_12_out & not_13_out & out_4;  // AND_Gate and_17, 32 bits wide
  assign and_18_out = {32{High_Low}} & not_13_out & out_4;  // AND_Gate and_18, 32 bits wide
  assign and_19_out = {32{High_Low}} & demultiplexer_4_out0 & not_14_out;  // AND_Gate and_19, 32 bits wide
  assign and_20_out = {32{High_Low}} & demultiplexer_4_out0 & out_4;  // AND_Gate and_20, 32 bits wide
  assign or_4_out = and_17_out | and_18_out | and_19_out | and_20_out;  // OR_Gate or_4, 32 bits wide
endmodule

module bcd_to_binary (
  input  in_1,
  input  in_2,
  input  [8:0] in_3,
  input  in_4,
  input  in_5,
  input  [8:0] in_6,
  output [15:0] out_7,
  output [15:0] out_8
);

  wire and_1_out, and_2_out, and_3_out, clock_1_out, clock_2_out, d_ff_1_qn, d_ff_2_qn, d_ff_3_q, d_ff_4_q,
       d_ff_5_q, d_ff_6_q, d_ff_7_q, keyboard_1_avail, keyboard_2_avail, not_1_out, or_1_out;
  wire [6:0] keyboard_1_data, keyboard_2_data, subtractor_1_out, subtractor_2_out;
  wire [15:0] adder_1_out, adder_2_out, adder_3_out, adder_4_out, adder_5_out, adder_6_out, multiplier_1_out,
       multiplier_2_out, multiplier_3_out, multiplier_4_out, multiplier_5_out, multiplier_6_out,
       multiplier_7_out, multiplier_8_out, register_1_q, register_2_q, register_3_q, register_4_q,
       register_6_q, register_7_q, register_8_q, register_9_q, undriven, undriven_2, undriven_3, undriven_4,
       undriven_5, undriven_6, undriven_7, undriven_8, undriven_9, undriven_10;

  Clock clock_1 (.out(clock_1_out));
  Keyboard keyboard_1 (.clk(and_1_out), .avail(keyboard_1_avail), .data(keyboard_1_data));  // open: re, clr
  and and_1 (and_1_out, in_5, keyboard_1_avail, clock_1_out);
  Clock clock_2 (.out(clock_2_out));
  D_Flip_Flop d_ff_1 (.clk(and_1_out), .D(in_4), .Qn(d_ff_1_qn));  // open: Q, preset, en, reset
  and and_2 (and_2_out, in_2, keyboard_2_avail, clock_2_out);
  Keyboard keyboard_2 (.clk(and_2_out), .avail(keyboard_2_avail), .data(keyboard_2_data));  // open: re, clr
  Subtractor #(.width(7)) subtractor_1 (
    .a(keyboard_1_data), .b(7'b0110000), .out(subtractor_1_out));  // open: bin, bout
  D_Flip_Flop d_ff_2 (.clk(and_2_out), .D(in_1), .Qn(d_ff_2_qn));  // open: Q, preset, en, reset
  Subtractor #(.width(7)) subtractor_2 (
    .a(keyboard_2_data), .b(7'b0110000), .out(subtractor_2_out));  // open: bin, bout
  Register #(.width(16)) register_1 (.D({in_6, subtractor_1_out}), .Q(register_1_q), .clk(and_1_out));  // open: en, clr
  Register #(.width(16)) register_2 (.D(register_1_q), .Q(register_2_q), .clk(and_1_out));  // open: en, clr
  Register #(.width(16)) register_3 (.D(register_2_q), .Q(register_3_q), .clk(and_1_out));  // open: en, clr
  Register #(.width(16)) register_4 (.D(register_3_q), .Q(register_4_q), .clk(and_1_out));  // open: en, clr
  Register #(.width(16)) register_5 (.D(register_4_q), .clk(and_1_out));  // open: en, Q, clr
  and and_3 (and_3_out, d_ff_2_qn, not_1_out);
  not not_1 (not_1_out, or_1_out);
  or or_1 (or_1_out, d_ff_3_q, d_ff_4_q, d_ff_7_q, d_ff_5_q, d_ff_6_q);
  D_Flip_Flop d_ff_3 (.clk(and_2_out), .D(and_3_out), .Q(d_ff_3_q));  // open: Qn, preset, en, reset
  D_Flip_Flop d_ff_4 (.clk(and_2_out), .D(d_ff_3_q), .Q(d_ff_4_q));  // open: Qn, preset, en, reset
  D_Flip_Flop d_ff_5 (.clk(and_2_out), .D(d_ff_4_q), .Q(d_ff_5_q));  // open: Qn, preset, en, reset
  D_Flip_Flop d_ff_6 (.clk(and_2_out), .D(d_ff_5_q), .Q(d_ff_6_q));  // open: Qn, preset, en, reset
  D_Flip_Flop d_ff_7 (.clk(and_2_out), .D(d_ff_6_q), .Q(d_ff_7_q));  // open: Qn, preset, en, reset
  Register #(.width(16)) register_6 (.D({in_3, subtractor_2_out}), .Q(register_6_q), .clk(and_2_out));  // open: en, clr
  Register #(.width(16)) register_7 (.D(register_6_q), .Q(register_7_q), .clk(and_2_out));  // open: en, clr
  Register #(.width(16)) register_8 (.D(register_7_q), .Q(register_8_q), .clk(and_2_out));  // open: en, clr
  Register #(.width(16)) register_9 (.D(register_8_q), .Q(register_9_q), .clk(and_2_out));  // open: en, clr
  Register #(.width(16)) register_10 (.D(register_9_q), .clk(and_2_out));  // open: en, Q, clr
  Multiplier #(.width(16)) multiplier_1 (.a(undriven_4), .b(16'ha), .out(multiplier_1_out));  // open: cin, cout
  Adder #(.width(16)) adder_1 (.a(multiplier_1_out), .b(undriven_2), .out(adder_1_out));  // open: cin, cout
  Multiplier #(.width(16)) multiplier_2 (.a(undriven_5), .b(16'ha), .out(multiplier_2_out));  // open: cin, cout
  Multiplier #(.width(16)) multiplier_3 (.a(adder_1_out), .b(16'ha), .out(multiplier_3_out));  // open: cin, cout
  Adder #(.width(16)) adder_2 (.a(multiplier_2_out), .b(undriven_3), .out(adder_2_out));  // open: cin, cout
  Adder #(.width(16)) adder_3 (.a(multiplier_3_out), .b(undriven_8), .out(adder_3_out));  // open: cin, cout
  Multiplier #(.width(16)) multiplier_4 (.a(adder_2_out), .b(16'ha), .out(multiplier_4_out));  // open: cin, cout
  Adder #(.width(16)) adder_4 (.a(multiplier_4_out), .b(undriven_10), .out(adder_4_out));  // open: cin, cout
  Multiplier #(.width(16)) multiplier_5 (.a(adder_3_out), .b(16'ha), .out(multiplier_5_out));  // open: cin, cout
  Multiplier #(.width(16)) multiplier_6 (.a(adder_4_out), .b(16'ha), .out(multiplier_6_out));  // open: cin, cout
  Adder #(.width(16)) adder_5 (.a(multiplier_5_out), .b(undriven_9), .out(adder_5_out));  // open: cin, cout
  Adder #(.width(16)) adder_6 (.a(multiplier_6_out), .b(undriven), .out(adder_6_out));  // open: cin, cout
  Multiplier #(.width(16)) multiplier_7 (.a(adder_5_out), .b(16'ha), .out(multiplier_7_out));  // open: cin, cout
  Multiplier #(.width(16)) multiplier_8 (.a(adder_6_out), .b(16'ha), .out(multiplier_8_out));  // open: cin, cout
  Adder #(.width(16)) adder_7 (.a(multiplier_7_out), .b(undriven_6), .out(out_7));  // open: cin, cout
  Adder #(.width(16)) adder_8 (.a(multiplier_8_out), .b(undriven_7), .out(out_8));  // open: cin, cout
endmodule
